# Fritzing sketch Meuhcube_extension_extension_set (saved by Fritzing 0.9.2b)

parts:
  U3 = XBEE-1 [package=xbee-silk]  # not connected
  J58 = double row female pin header, 20 pins [form="♀ (female)"]

nets:
  5V: J58.pin1
  AREF: J58.pin2
  MOSI: J58.pin3
  SS: J58.pin4
  RX1: J58.pin5
  RX2: J58.pin6
  RX3: J58.pin7
  Vin: J58.pin8
  SCL: J58.pin9
  GND: J58.pin10, J58.pin11
  SDA: J58.pin12
  RESET: J58.pin13
  TX3: J58.pin14
  TX2: J58.pin15
  TX1: J58.pin16
  SCLK: J58.pin17
  MISO: J58.pin18
  IOREF: J58.pin19
  3.3v: J58.pin20
