# Fritzing sketch Meuhcube_main_v1_rc (saved by Fritzing 0.9.3b)
circuit board: 11.55cm x 11.55cm

parts:
  Arduino_MEGA = Arduino Mega 2560 (Rev3)
  J1 = female pin header, 1 pin [form="♀ (female)"]
  J2 = female pin header, 1 pin [form="♀ (female)"]
  L1 = female pin header, 1 pin [form="♀ (female)"]
  L2 = female pin header, 1 pin [form="♀ (female)"]
  L3 = female pin header, 1 pin [form="♀ (female)"]
  L4 = female pin header, 1 pin [form="♀ (female)"]
  L5 = female pin header, 1 pin [form="♀ (female)"]
  L6 = female pin header, 1 pin [form="♀ (female)"]
  L7 = female pin header, 1 pin [form="♀ (female)"]
  J10 = female pin header, 1 pin [form="♀ (female)"]
  J11 = female pin header, 1 pin [form="♀ (female)"]
  J12 = female pin header, 1 pin [form="♀ (female)"]
  J13 = female pin header, 1 pin [form="♀ (female)"]
  J14 = female pin header, 1 pin [form="♀ (female)"]
  J15 = female pin header, 1 pin [form="♀ (female)"]
  J16 = female pin header, 1 pin [form="♀ (female)"]
  J17 = female pin header, 1 pin [form="♀ (female)"]
  J18 = female pin header, 1 pin [form="♀ (female)"]
  J19 = female pin header, 1 pin [form="♀ (female)"]
  J20 = female pin header, 1 pin [form="♀ (female)"]
  J21 = female pin header, 1 pin [form="♀ (female)"]
  J22 = female pin header, 1 pin [form="♀ (female)"]
  J23 = female pin header, 1 pin [form="♀ (female)"]
  J24 = female pin header, 1 pin [form="♀ (female)"]
  J25 = female pin header, 1 pin [form="♀ (female)"]
  J26 = female pin header, 1 pin [form="♀ (female)"]
  J27 = female pin header, 1 pin [form="♀ (female)"]
  J28 = female pin header, 1 pin [form="♀ (female)"]
  J29 = female pin header, 1 pin [form="♀ (female)"]
  J30 = female pin header, 1 pin [form="♀ (female)"]
  J31 = female pin header, 1 pin [form="♀ (female)"]
  J32 = female pin header, 1 pin [form="♀ (female)"]
  J33 = female pin header, 1 pin [form="♀ (female)"]
  J34 = female pin header, 1 pin [form="♀ (female)"]
  J35 = female pin header, 1 pin [form="♀ (female)"]
  J36 = female pin header, 1 pin [form="♀ (female)"]
  J37 = female pin header, 1 pin [form="♀ (female)"]
  J38 = female pin header, 1 pin [form="♀ (female)"]
  J39 = female pin header, 1 pin [form="♀ (female)"]
  J40 = female pin header, 1 pin [form="♀ (female)"]
  J41 = female pin header, 1 pin [form="♀ (female)"]
  J42 = female pin header, 1 pin [form="♀ (female)"]
  J43 = female pin header, 1 pin [form="♀ (female)"]
  J44 = female pin header, 1 pin [form="♀ (female)"]
  J45 = female pin header, 1 pin [form="♀ (female)"]
  J46 = female pin header, 1 pin [form="♀ (female)"]
  J47 = female pin header, 1 pin [form="♀ (female)"]
  J48 = female pin header, 1 pin [form="♀ (female)"]
  J49 = female pin header, 1 pin [form="♀ (female)"]
  J50 = female pin header, 1 pin [form="♀ (female)"]
  J51 = female pin header, 1 pin [form="♀ (female)"]
  J52 = female pin header, 1 pin [form="♀ (female)"]
  J53 = female pin header, 1 pin [form="♀ (female)"]
  J54 = female pin header, 1 pin [form="♀ (female)"]
  J55 = female pin header, 1 pin [form="♀ (female)"]
  J56 = female pin header, 1 pin [form="♀ (female)"]
  Q61 = MOSFET-NCHANNEL [package=sot23-3]
  Q60 = MOSFET-NCHANNEL [package=sot23-3]
  Q59 = MOSFET-NCHANNEL [package=sot23-3]
  Q58 = MOSFET-NCHANNEL [package=sot23-3]
  Q48 = MOSFET-NCHANNEL [package=sot23-3]
  Q47 = MOSFET-NCHANNEL [package=sot23-3]
  Q46 = MOSFET-NCHANNEL [package=sot23-3]
  Q45 = MOSFET-NCHANNEL [package=sot23-3]
  Q44 = MOSFET-NCHANNEL [package=sot23-3]
  Q43 = MOSFET-NCHANNEL [package=sot23-3]
  Q42 = MOSFET-NCHANNEL [package=sot23-3]
  Q41 = MOSFET-NCHANNEL [package=sot23-3]
  Q40 = MOSFET-NCHANNEL [package=sot23-3]
  Q39 = MOSFET-NCHANNEL [package=sot23-3]
  Q38 = MOSFET-NCHANNEL [package=sot23-3]
  Q37 = MOSFET-NCHANNEL [package=sot23-3]
  Q33 = MOSFET-NCHANNEL [package=sot23-3]
  Q32 = MOSFET-NCHANNEL [package=sot23-3]
  Q31 = MOSFET-NCHANNEL [package=sot23-3]
  Q26 = MOSFET-NCHANNEL [package=sot23-3]
  Q25 = MOSFET-NCHANNEL [package=sot23-3]
  Q24 = MOSFET-NCHANNEL [package=sot23-3]
  Q23 = MOSFET-NCHANNEL [package=sot23-3]
  Q21 = MOSFET-NCHANNEL [package=sot23-3]
  Q20 = MOSFET-NCHANNEL [package=sot23-3]
  Q18 = MOSFET-NCHANNEL [package=sot23-3]
  Q11 = MOSFET-NCHANNEL [package=sot23-3]
  Q64 = MOSFET-NCHANNEL [package=sot23-3]
  Q62 = MOSFET-NCHANNEL [package=sot23-3]
  Q57 = MOSFET-NCHANNEL [package=sot23-3]
  Q56 = MOSFET-NCHANNEL [package=sot23-3]
  Q55 = MOSFET-NCHANNEL [package=sot23-3]
  Q54 = MOSFET-NCHANNEL [package=sot23-3]
  Q53 = MOSFET-NCHANNEL [package=sot23-3]
  Q52 = MOSFET-NCHANNEL [package=sot23-3]
  Q51 = MOSFET-NCHANNEL [package=sot23-3]
  Q50 = MOSFET-NCHANNEL [package=sot23-3]
  Q49 = MOSFET-NCHANNEL [package=sot23-3]
  Q36 = MOSFET-NCHANNEL [package=sot23-3]
  Q35 = MOSFET-NCHANNEL [package=sot23-3]
  Q34 = MOSFET-NCHANNEL [package=sot23-3]
  Q29 = MOSFET-NCHANNEL [package=sot23-3]
  Q28 = MOSFET-NCHANNEL [package=sot23-3]
  Q27 = MOSFET-NCHANNEL [package=sot23-3]
  Q22 = MOSFET-NCHANNEL [package=sot23-3]
  Q2 = MOSFET-NCHANNEL [package=sot23-3]
  Q63 = MOSFET-NCHANNEL [package=sot23-3]
  Q19 = MOSFET-NCHANNEL [package=sot23-3]
  Q30 = MOSFET-NCHANNEL [package=sot23-3]
  U1 = ADP2300 [package=tsot]
  R2 = Resistor [tolerance=±5% resistance=220 package="0603 [SMD]"]
  R1 = Resistor [tolerance=±5% resistance=220 package="0603 [SMD]"]
  R3 = Resistor [tolerance=±5% resistance=10k package="0603 [SMD]"]
  C3 = Capacitor [package=0805]
  D1 = DIODE-SCHOTTKY [package=sma-diode]
  C1 = Capacitor [package=0603-cap]
  C2 = Capacitor [package=0805]
  U2 = TS391 [package=sot23-5]
  I1 = Inductors [package=SRR7032]
  R4 = Resistor [tolerance=±5% resistance=220 package="0402 [SMD]"]
  Q66 = TRANSISTOR_NPN [package=sot23-3]
  Q67 = TRANSISTOR_NPN [package=sot23-3]
  R6 = Resistor [tolerance=±5% resistance=220 package="0402 [SMD]"]
  R7 = Resistor [tolerance=±5% resistance=220 package="0402 [SMD]"]
  Q68 = TRANSISTOR_NPN [package=sot23-3]
  R8 = Resistor [tolerance=±5% resistance=220 package="0402 [SMD]"]
  Q69 = TRANSISTOR_NPN [package=sot23-3]
  R9 = Resistor [tolerance=±5% resistance=220 package="0402 [SMD]"]
  Q70 = TRANSISTOR_NPN [package=sot23-3]
  R10 = Resistor [tolerance=±5% resistance=220 package="0402 [SMD]"]
  Q71 = TRANSISTOR_NPN [package=sot23-3]
  R11 = Resistor [tolerance=±5% resistance=220 package="0402 [SMD]"]
  Q72 = TRANSISTOR_NPN [package=sot23-3]
  J58 = double row female pin header, 20 pins [form="♀ (female)"]

nets:
  PIN_X5Y4: Arduino_MEGA.A8, Q52.G
  PIN_X3Y5: Arduino_MEGA.A9, Q44.G
  PIN_X2Y5: Arduino_MEGA.A10, Q55.G
  PIN_X3Y6: Arduino_MEGA.A11, Q58.G
  PIN_X4Y6: Arduino_MEGA.A12, Q61.G
  PIN_X2Y6: Arduino_MEGA.A13, Q64.G
  PIN_X1Y5: Arduino_MEGA.A14, Q45.G
  PIN_X1Y6: Arduino_MEGA.A15, Q59.G
  PIN_X6Y5: Arduino_MEGA.A0, Q46.G
  PIN_X5Y5: Arduino_MEGA.A1, Q51.G
  PIN_X4Y5: Arduino_MEGA.A2, Q48.G
  PIN_X6Y6: Arduino_MEGA.A3, Q60.G
  PIN_X5Y6: Arduino_MEGA.A4, Q62.G
  PIN_X4Y4: Arduino_MEGA.A5, Q42.G
  PIN_X3Y4: Arduino_MEGA.A6, Q39.G
  PIN_X2Y4: Arduino_MEGA.A7, Q50.G
  SCL: Arduino_MEGA.D21/SCL, Arduino_MEGA.SCL, J58.pin9
  SDA: Arduino_MEGA.D20/SDA, Arduino_MEGA.SDA, J58.pin12
  RX1: Arduino_MEGA.D19/RX1, J58.pin5
  TX1: Arduino_MEGA.D18/TX1, J58.pin16
  RX2: Arduino_MEGA.D17_PWM/RX2, J58.pin6
  TX2: Arduino_MEGA.D16_PWM/TX2, J58.pin15
  RX3: Arduino_MEGA.D15/RX3, J58.pin7
  TX3: Arduino_MEGA.D14/TX3, J58.pin14
  AREF: Arduino_MEGA.AREF, J58.pin2
  GND: Arduino_MEGA.GND, U1.GND, R2.Pin_0, C3.2, D1.A, C2.2, U2.V-, Q66.C, Q67.C, Q68.C, Q69.C, Q70.C, Q71.C, Q72.C, J58.pin10, J58.pin11
  PIN_X6Y1: Arduino_MEGA.D13_PWM, Q24.G
  PIN_L4: Arduino_MEGA.D12_PWM, R7.Pin_0
  PIN_L5: Arduino_MEGA.D11_PWM, R8.Pin_0
  PIN_X0Y6: Arduino_MEGA.D10_PWM, Q63.G
  PIN_X0Y5: Arduino_MEGA.D9_PWM, Q53.G
  PIN_X5Y1: Arduino_MEGA.D8_PWM, Q28.G
  IOREF: Arduino_MEGA.IOREF, J58.pin19
  RESET: Arduino_MEGA.RESET, J58.pin13
  3.3v: Arduino_MEGA.3V3, J58.pin20
  5V: Arduino_MEGA.5V, R3.Pin_0, U2.-IN, J58.pin1
  Vin: Arduino_MEGA.VIN, U1.VIN, C2.1, U2.+IN, U2.V+, J58.pin8
  PIN_X2Y1: Arduino_MEGA.D2_PWM, Q29.G
  PIN_X0Y2: Arduino_MEGA.D3_PWM, Q36.G
  PIN_X3Y1: Arduino_MEGA.D4_PWM, Q26.G
  PIN_X0Y3: Arduino_MEGA.D5_PWM, Q49.G
  PIN_X4Y1: Arduino_MEGA.D6_PWM, Q25.G
  PIN_X0Y4: Arduino_MEGA.D7_PWM, Q54.G
  PIN_X1Y1: Arduino_MEGA.D22, Q23.G
  PIN_X0Y1: Arduino_MEGA.D23, Q27.G
  PIN_X2Y2: Arduino_MEGA.D24, Q34.G
  PIN_X1Y2: Arduino_MEGA.D25, Q31.G
  PIN_X3Y2: Arduino_MEGA.D26, Q32.G
  PIN_X1Y3: Arduino_MEGA.D27, Q37.G
  PIN_X4Y2: Arduino_MEGA.D28, Q30.G
  PIN_X1Y4: Arduino_MEGA.D29, Q47.G
  PIN_X5Y2: Arduino_MEGA.D30, Q35.G
  PIN_L6: Arduino_MEGA.D31, R9.Pin_0
  PIN_X6Y2: Arduino_MEGA.D32, Q33.G
  PIN_X0Y0: Arduino_MEGA.D33, Q2.G
  PIN_X6Y3: Arduino_MEGA.D34, Q38.G
  PIN_X2Y0: Arduino_MEGA.D35, Q19.G
  PIN_X2Y3: Arduino_MEGA.D36, Q57.G
  PIN_X1Y0: Arduino_MEGA.D37, Q11.G
  PIN_X3Y3: Arduino_MEGA.D38, Q41.G
  PIN_X3Y0: Arduino_MEGA.D39, Q18.G
  PIN_X4Y3: Arduino_MEGA.D40, Q40.G
  PIN_X4Y0: Arduino_MEGA.D41, Q20.G
  PIN_X5Y3: Arduino_MEGA.D42, Q56.G
  PIN_X5Y0: Arduino_MEGA.D43, Q22.G
  PIN_X6Y4: Arduino_MEGA.D44, Q43.G
  PIN_L1: Arduino_MEGA.D45, R11.Pin_0
  PIN_L3: Arduino_MEGA.D46, R6.Pin_0
  PIN_X6Y0: Arduino_MEGA.D47, Q21.G
  PIN_L2: Arduino_MEGA.D48, R4.Pin_0
  PIN_L0: Arduino_MEGA.D49, R10.Pin_1
  MISO: Arduino_MEGA.D50, J58.pin18
  MOSI: Arduino_MEGA.D51, J58.pin3
  SCLK: Arduino_MEGA.D52, J58.pin17
  SS: Arduino_MEGA.D53, J58.pin4
  N1: J1.pin1, Q2.S
  N2: J2.pin1, Q11.S
  N3: L1.pin1, Q71.E
  N4: L2.pin1, Q72.E
  N5: L3.pin1, Q67.E
  N6: L4.pin1, Q66.E
  N7: L5.pin1, Q68.E
  N8: L6.pin1, Q69.E
  N9: L7.pin1, Q70.E
  N10: J10.pin1, Q19.S
  N11: J11.pin1, Q18.S
  N12: J12.pin1, Q21.S
  N13: J13.pin1, Q22.S
  N14: J14.pin1, Q20.S
  N15: J15.pin1, Q27.S
  N16: J16.pin1, Q29.S
  N17: J17.pin1, Q28.S
  N18: J18.pin1, Q23.S
  N19: J19.pin1, Q25.S
  N20: J20.pin1, Q24.S
  N21: J21.pin1, Q26.S
  N22: J22.pin1, Q34.S
  N23: J23.pin1, Q32.S
  N24: J24.pin1, Q33.S
  N25: J25.pin1, Q31.S
  N26: J26.pin1, Q30.S
  N27: J27.pin1, Q35.S
  N28: J28.pin1, Q36.S
  N29: J29.pin1, Q49.S
  N30: J30.pin1, Q40.S
  N31: J31.pin1, Q53.S
  N32: J32.pin1, Q56.S
  N33: J33.pin1, Q48.S
  N34: J34.pin1, Q54.S
  N35: J35.pin1, Q51.S
  N36: J36.pin1, Q39.S
  N37: J37.pin1, Q52.S
  N38: J38.pin1, Q47.S
  N39: J39.pin1, Q44.S
  N40: J40.pin1, Q57.S
  N41: J41.pin1, Q41.S
  N42: J42.pin1, Q37.S
  N43: J43.pin1, Q55.S
  N44: J44.pin1, Q45.S
  N45: J45.pin1, Q43.S
  N46: J46.pin1, Q38.S
  N47: J47.pin1, Q50.S
  N48: J48.pin1, Q46.S
  N49: J49.pin1, Q42.S
  N50: J50.pin1, Q62.S
  N51: J51.pin1, Q58.S
  N52: J52.pin1, Q60.S
  N53: J53.pin1, Q59.S
  N54: J54.pin1, Q61.S
  N55: J55.pin1, Q63.S
  N56: J56.pin1, Q64.S
  3.3V: Q61.D, Q60.D, Q59.D, Q58.D, Q48.D, Q47.D, Q46.D, Q45.D, Q44.D, Q43.D, Q42.D, Q41.D, Q40.D, Q39.D, Q38.D, Q37.D, Q33.D, Q32.D, Q31.D, Q26.D, Q25.D, Q24.D, Q23.D, Q21.D, Q20.D, Q18.D, Q11.D, Q64.D, Q62.D, Q57.D, Q56.D, Q55.D, Q54.D, Q53.D, Q52.D, Q51.D, Q50.D, Q49.D, Q36.D, Q35.D, Q34.D, Q29.D, Q28.D, Q27.D, Q22.D, Q2.D, Q63.D, Q19.D, Q30.D, R1.Pin_1, C3.1, I1.2
  BST: U1.BST, C1.1
  N57: U1.FB, R2.Pin_1, R1.Pin_0
  EN: U1.EN, R3.Pin_1, U2.OUT
  N58: U1.SW, D1.C, C1.2, I1.1
  N59: R4.Pin_1, Q67.B
  N60: Q66.B, R6.Pin_1
  N61: R7.Pin_1, Q68.B
  N62: R8.Pin_1, Q69.B
  N63: R9.Pin_1, Q70.B
  N64: R10.Pin_0, Q71.B
  N65: R11.Pin_1, Q72.B

notes:
  INFOS COMPOSANTS
  49 leds maxi soit 0.2 mA x 49 = 980 mA
  comparateur : TS391ILT
  regulateur : ADP2301AUJZ-R7
  inductance : 2333955
  C1 : 2496384 / 0603, 0.1 uF
  C2 : 2320833 / 0805, 10 uF
  C3 : 1759415 / 0805, 22 uF
  D1 : 1843686
  R1 : 1170937 - 31.6 kOhms
  R2 et R3 : 1170889 - 10.2 kOhms
  Connecteurs :
  2356202 (AD)
  ou 2356139 (male)
  ou 1593495 (femelle)
  Meuhcube v1.0

custom parts:
  ADP2300: DC to DC stepdown regulator
